# Fritzing sketch Single_Extruder (saved by Fritzing 0.9.3b)

parts:
  Part1 = Arduino Nano (Rev3.0)
  M1 = Stepper Motor - Bipolar
  Power_plug2 = Power plug
  Part3 = EasyDriver_v44
  U1 = AD5330 [package=tssop20]

nets:
  GND: Part1.GND, Power_plug2.GND, Part3.GND
  N1: Part1.D6, Part3.DIR
  N2: Part1.D7, Part3.STEP
  N3: Part1.D8, Part3.ENABLE
  N4: Part1.D9, Part3.SLEEP
  N5: Part1.A7, U1.VDD
  N6: M1.A, Part3.OUT2A
  N7: M1.C, Part3.OUT1A
  N8: M1.B, Part3.OUT2B
  N9: M1.D, Part3.OUT1B
  N10: Power_plug2.VCC, Part3.V+

// code stored in the sketch: Single_Extruder.ino
// Arduino NANO

#include <SPI.h>

volatile byte state = true;
const byte interruptPin = 2;

const int st_1 = 4;
const int dr_1 = 5;
const int en_1 = 8;
const int sl_1 = A2;

volatile int spd_2 = 500;
int actual_spd_1 = 500;
unsigned long t_1;

void setup() {
	Serial.begin(9600);
  pinMode(st_1, OUTPUT);
  pinMode(en_1, OUTPUT);
  pinMode(dr_1, OUTPUT);
  pinMode(sl_1, OUTPUT);

  digitalWrite(dr_1, HIGH);
  digitalWrite(sl_1, LOW);
  digitalWrite(en_1, LOW);


  pinMode(interruptPin, INPUT);

  attachInterrupt(digitalPinToInterrupt(interruptPin),
                  motorsState, CHANGE);
	
	state = digitalRead(interruptPin);
  t_1 = micros();
}

void loop() {
  if (state) {
    if (micros() - t_1 > spd_1) {
      t_1 = micros();
      digitalWrite(st_1, HIGH);
    }
    else if (micros() - t_1 > 50) {
      digitalWrite(st_1, LOW);
    }    
  }
}

void motorsState() {
  state = !digitalRead(interruptPin);

  if (state) {
    digitalWrite(sl_1, LOW);
    digitalWrite(sl_2, LOW);
  } else {
    digitalWrite(sl_1, HIGH);
    digitalWrite(sl_2, HIGH);
  }

  Serial.print("Working?");
  Serial.print("\t");
  Serial.print(state);
  Serial.println();
}

// code stored in the sketch: SPI_Master.ino
// Arduino UNO: Reading the signals and sending over SPI.

#include <SPI.h>

int pVal = 0;


void setup() {
  pinMode(SS, OUTPUT);
  digitalWrite(SS, HIGH);
  SPI.begin();
  SPI.setClockDivider(SPI_CLOCK_DIV8);
  
  pinMode(2, INPUT);
  pinMode(3, INPUT);
  pinMode(4, INPUT);
  pinMode(5, INPUT);
  pinMode(6, INPUT);
  pinMode(7, INPUT);
  pinMode(8, INPUT);

//  Serial.begin(115200);
}

void loop() {
  int val = 0;
  for(int i = 8; i > 1; i--){
    val = val << 1 | !digitalRead(i);
  }
//  Serial.println(val);
  // Serial.println(val);
  if (val != pVal){
    
    pVal = val;
    digitalWrite(SS, LOW);
    SPI.transfer(val);
    digitalWrite(SS, HIGH);
  }
}

// code stored in the sketch: SPI_Slave.ino
// Arduino NANO

#include <SPI.h>

volatile byte state = true;
const byte interruptPin = 2;

const int st_1 = 4;
const int dr_1 = 5;
const int st_2 = 6;
const int dr_2 = 7;
const int en_1 = 8;
const int en_2 = 9;
const int sl_1 = A2;
const int sl_2 = A3;


volatile int spd_1 = 500;
volatile int spd_2 = 500;
int actual_spd_1 = 500;
int actual_spd_2 = 500;
unsigned long t_1, t_2;


void setup() {
  Serial.begin(9600);
  pinMode(st_1, OUTPUT);
  pinMode(st_2, OUTPUT);
  pinMode(en_1, OUTPUT);
  pinMode(en_2, OUTPUT);
  pinMode(dr_1, OUTPUT);
  pinMode(dr_2, OUTPUT);
  pinMode(sl_1, OUTPUT);
  pinMode(sl_2, OUTPUT);

  digitalWrite(dr_1, HIGH);
  digitalWrite(dr_2, HIGH);

  digitalWrite(sl_1, LOW);
  digitalWrite(sl_2, LOW);

  digitalWrite(en_1, LOW);
  digitalWrite(en_2, LOW);

  pinMode(MISO, OUTPUT);
  SPCR |= _BV(SPE);
  SPI.attachInterrupt();

  pinMode(interruptPin, INPUT);

  attachInterrupt(digitalPinToInterrupt(interruptPin),
                  motorsState, CHANGE);

  t_1 = micros();
  t_2 = micros();
}

void loop() {
  if (actual_spd_1 > spd_1){
    actual_spd_1--;
  } else if (actual_spd_1 < spd_1) {
    actual_spd_1++;
  }
  
  if (actual_spd_2 > spd_2){
    actual_spd_2--;
  } else if (actual_spd_2 < spd_2) {
    actual_spd_2++;
  }
  
  if (state) {
    if (micros() - t_1 > spd_1) {
      t_1 = micros();
      digitalWrite(st_1, HIGH);
    }
    else if (micros() - t_1 > 50) {
      digitalWrite(st_1, LOW);
    }
    
    if (micros() - t_2 > spd_2) {
      t_2 = micros();
      digitalWrite(st_2, HIGH);
    }
    else if (micros() - t_2 > 50) {
      digitalWrite(st_2, LOW);
    }
  }
}

void motorsState() {
  state = !digitalRead(interruptPin);

  if (state) {
    digitalWrite(sl_1, LOW);
    digitalWrite(sl_2, LOW);
  } else {
    digitalWrite(sl_1, HIGH);
    digitalWrite(sl_2, HIGH);
  }

  Serial.print("Working?");
  Serial.print("\t");
  Serial.print(state);
  Serial.println();
}


ISR(SPI_STC_vect) {
  spd_1 = int(SPDR);
  spd_2 = 127 - spd_1;

  Serial.print(spd_1);
  Serial.print("\t");
  Serial.print(spd_2);
  Serial.print("\t\t");


  spd_1 = map(spd_1, 0, 127, 100, 1500);
  spd_2 = map(spd_2, 0, 127, 100, 1500);

  Serial.print(spd_1);
  Serial.print("\t");
  Serial.print(spd_2);
  Serial.print("\t");
  Serial.println();
}
